# Fritzing sketch schematics (saved by Fritzing 0.9.6b)
# CH340G Copyrights: Creative Commons Attribution-ShareAlike License
breadboards: 1

parts:
  U1 = atmega328 [package=dip]
  IC1 = CH340G [chip_label=CH340 package=SO]
  X1 = USB Connectors [package=usb-a-pcb]
  C1 = Capacitor [package=cap-pth-small]
  C2 = Capacitor [package=cap-pth-small]
  C3 = Capacitor [package=cap-pth-small]
  Y1 = CRYSTAL [package=hc49us]
  part = SWITCH-MOMENTARY-2 [package=tactile-pth]
  LED1 = LEDs [package=fkit-led-1206]

nets:
  N1: U1.RESET, IC1.DTR#
  N2: U1.D0_(RX), IC1.TXD
  N3: U1.D1_(TX), IC1.RXD
  VCC: U1.VCC, U1.AVCC, U1.AREF, IC1.VCC, X1.D+, C1.2
  GND: U1.GND, IC1.GND, X1.GND, C1.1, C2.2, C3.2, part.2, LED1.C
  N4: U1.D12, part.1
  N5: U1.D13, LED1.A
  N6: IC1.UD+, X1.D-
  N7: IC1.UD-, X1.VBUS
  N8: IC1.XI, C2.1, Y1.1
  N9: IC1.XO, C3.1, Y1.2

custom parts:
  CH340G: Fritzing SO16 IC CH340 is a series of USB bus adapters, that provides serial, parallel or IrDA interfaces over the USB bus (note: CH340G supports serial interface only). The CH340G integrate circuit provides common MODEM signals to allow adding a UART to a computer, or converting existing UART devices to USB interface. An English datasheet is available at: https://www.insidegadgets.com/wp-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
